# Fritzing sketch Схема (saved by Fritzing 0.9.5d)

parts:
  MFRC522 = RFID RC522
  Пищалка = Buzzer
  Arduino = Arduino Nano (Rev3.0)

nets:
  N1: MFRC522.SDA, Arduino.D10
  N2: MFRC522.SCK, Arduino.D13/SCK
  N3: MFRC522.MOSI, Arduino.D11/MOSI
  N4: MFRC522.MISO, Arduino.D12/MISO
  GND: MFRC522.GND, Пищалка.pin2, Arduino.GND
  N5: MFRC522.RST, Arduino.D9
  VCC: MFRC522.VCC, Arduino.3V3
  N6: Пищалка.pin1, Arduino.D8
